// Logisim project 1bfa.circ as structural Verilog: 5 circuits, main circuit 1bfa
module _1bfa (
  input  A,
  input  B,
  input  cin,
  output Sum,
  output co
);

  wire and_1_out, and_2_out, and_3_out, xor_1_out;

  xor xor_1 (xor_1_out, A, B);
  and and_1 (and_1_out, A, B);
  and and_2 (and_2_out, A, cin);
  and and_3 (and_3_out, B, cin);
  xor xor_2 (Sum, xor_1_out, cin);
  or or_1 (co, and_1_out, and_3_out);
endmodule

module _4bfa (
  input  [3:0] in_1,
  input  [3:0] in_2,
  input  in_3,
  output [3:0] out_4,
  output out_5
);

  wire n1bfa_2_co, n1bfa_3_co, n1bfa_4_co;

  _1bfa u_1bfa_1 (.A(in_1[3]), .B(in_2[3]), .cin(n1bfa_2_co), .Sum(out_4[3]), .co(out_5));
  _1bfa u_1bfa_2 (.A(in_1[2]), .B(in_2[2]), .cin(n1bfa_3_co), .Sum(out_4[2]), .co(n1bfa_2_co));
  _1bfa u_1bfa_3 (.A(in_1[1]), .B(in_2[1]), .cin(n1bfa_4_co), .Sum(out_4[1]), .co(n1bfa_3_co));
  _1bfa u_1bfa_4 (.A(in_1[0]), .B(in_2[0]), .cin(in_3), .Sum(out_4[0]), .co(n1bfa_4_co));
endmodule

// add32
module _32bfa (
  input  [31:0] in_1,
  input  [31:0] in_2,
  input  in_3,
  output out_4,
  output [31:0] out_5
);

  wire n4bfa_2_out_5, n4bfa_3_out_5, n4bfa_4_out_5, n4bfa_5_out_5, n4bfa_6_out_5, n4bfa_7_out_5,
       n4bfa_8_out_5;

  _4bfa u_4bfa_1 (.in_1(in_1[31:28]), .in_2(in_2[31:28]), .out_4(out_5[31:28]), .out_5(out_4), .in_3(n4bfa_2_out_5));
  _4bfa u_4bfa_2 (
    .in_1(in_1[27:24]), .in_2(in_2[27:24]), .out_4(out_5[27:24]), .out_5(n4bfa_2_out_5), .in_3(n4bfa_3_out_5));
  _4bfa u_4bfa_3 (
    .in_1(in_1[23:20]), .in_2(in_2[23:20]), .out_4(out_5[23:20]), .out_5(n4bfa_3_out_5), .in_3(n4bfa_4_out_5));
  _4bfa u_4bfa_4 (
    .in_1(in_1[19:16]), .in_2(in_2[19:16]), .out_4(out_5[19:16]), .out_5(n4bfa_4_out_5), .in_3(n4bfa_5_out_5));
  _4bfa u_4bfa_5 (
    .in_1(in_1[15:12]), .in_2(in_2[15:12]), .out_4(out_5[15:12]), .out_5(n4bfa_5_out_5), .in_3(n4bfa_6_out_5));
  _4bfa u_4bfa_6 (
    .in_1(in_1[11:8]), .in_2(in_2[11:8]), .out_4(out_5[11:8]), .out_5(n4bfa_6_out_5), .in_3(n4bfa_7_out_5));
  _4bfa u_4bfa_7 (.in_1(in_1[7:4]), .in_2(in_2[7:4]), .out_4(out_5[7:4]), .out_5(n4bfa_7_out_5), .in_3(n4bfa_8_out_5));
  _4bfa u_4bfa_8 (.in_1(in_1[3:0]), .in_2(in_2[3:0]), .out_4(out_5[3:0]), .out_5(n4bfa_8_out_5), .in_3(in_3));
endmodule

// sub32
module _32bfs (
  input  [31:0] in_1,
  input  [31:0] in_2,
  input  in_3,
  output [31:0] out_4,
  output out_5
);

  wire [31:0] n32bfa_1_out_5, not_1_out;

  assign not_1_out = ~in_1;  // NOT_Gate not_1, 32 bits wide
  _32bfa u_32bfa_1 (.in_1(not_1_out), .in_2(in_2), .out_5(n32bfa_1_out_5), .out_4(out_5), .in_3(in_3));
  assign out_4 = ~n32bfa_1_out_5;  // NOT_Gate not_2, 32 bits wide
endmodule

module alu (
  input  in_1,
  input  [31:0] in_2,
  input  [31:0] in_3,
  input  [1:0] in_4,
  output out_5,
  output [31:0] out_6,
  output out_7
);

  wire n32bfa_1_out_4, n32bfs_1_out_5;
  wire [31:0] and_1_out, n32bfa_1_out_5, n32bfs_1_out_4, or_1_out;

  _32bfa u_32bfa_1 (.in_1(in_2), .in_2(in_3), .out_5(n32bfa_1_out_5), .out_4(n32bfa_1_out_4), .in_3(in_1));
  _32bfs u_32bfs_1 (.in_1(in_2), .in_2(in_3), .in_3(in_1), .out_4(n32bfs_1_out_4), .out_5(n32bfs_1_out_5));
  assign and_1_out = in_2 & in_3;  // AND_Gate and_1, 32 bits wide
  assign or_1_out = in_2 | in_3;  // OR_Gate or_1, 32 bits wide
  Multiplexer #(.select(2), .width(32)) multiplexer_1 (
    .in0(n32bfa_1_out_5), .in1(n32bfs_1_out_4), .in2(and_1_out), .in3(or_1_out), .out(out_6), .sel(in_4));  // open: en
  Multiplexer #(.select(2)) multiplexer_2 (
    .in0(n32bfa_1_out_4), .in1(n32bfs_1_out_5), .in2(1'b0), .in3(1'b0), .out(out_5), .sel(in_4));  // open: en
  nor nor_1 (out_7, out_6[0], out_6[1], out_6[2], out_6[3], out_6[4], out_6[5], out_6[6], out_6[7], out_6[8], out_6[9], out_6[10], out_6[11], out_6[12], out_6[13], out_6[14], out_6[16], out_6[17], out_6[18], out_6[19], out_6[20], out_6[21], out_6[22], out_6[23], out_6[24], out_6[25], out_6[26], out_6[27], out_6[28], out_6[29], out_6[30], out_6[31]);
endmodule
