// Logisim project 7_MIPS.circ as structural Verilog: 1 circuit, main circuit 7_MIPS
module _7_MIPS (
  input  [11:0] in_1,
  output [6:0] out_2
);

  wire decoder_1_out0, decoder_1_out1, decoder_1_out4, decoder_1_out5, decoder_2_out0, decoder_2_out3,
       decoder_2_out4, decoder_2_out5, decoder_2_out7, decoder_3_out4, decoder_4_out1, decoder_4_out3;

  Decoder #(.select(3)) decoder_1 (
    .out0(decoder_1_out0), .out1(decoder_1_out1), .out4(decoder_1_out4), .out5(decoder_1_out5),
    .sel(in_1[11:9]));  // open: out2, out3, out6, out7, en
  Decoder #(.select(3)) decoder_2 (
    .out0(decoder_2_out0), .out3(decoder_2_out3), .out4(decoder_2_out4), .out5(decoder_2_out5),
    .out7(decoder_2_out7), .sel(in_1[8:6]));  // open: out1, out2, out6, en
  Decoder #(.select(3)) decoder_3 (
    .out4(decoder_3_out4), .sel(in_1[5:3]));  // open: out0, out1, out2, out3, out5, out6, out7, en
  Decoder #(.select(3)) decoder_4 (
    .out1(decoder_4_out1), .out3(decoder_4_out3), .sel(in_1[2:0]));  // open: out0, out2, out4, out5, out6, out7, en
  and and_1 (out_2[6], decoder_1_out0, decoder_2_out0, decoder_3_out4, decoder_4_out1);
  and and_2 (out_2[5], decoder_1_out0, decoder_2_out0, decoder_3_out4, decoder_4_out3);
  and and_3 (out_2[4], decoder_1_out1, decoder_2_out5);
  and and_4 (out_2[3], decoder_1_out1, decoder_2_out7);
  and and_5 (out_2[2], decoder_1_out4, decoder_2_out3);
  and and_6 (out_2[1], decoder_1_out5, decoder_2_out3);
  and and_7 (out_2[0], decoder_2_out4, decoder_1_out0);
endmodule
