// Logisim project Encoder.circ as structural Verilog: 9 circuits, main circuit Encoder
// Encoder-18074102
module ENUNIT (
  input  Cin,
  input  [31:0] A,
  input  [31:0] B,
  input  [15:0] imm16,
  input  [5:0] opcode,
  input  [5:0] funct,
  output Cout,
  output [31:0] out,
  output PC_sel
);

  wire alu_1_zero, encoder_1_b_sel;
  wire [1:0] encoder_1_alu_sel, encoder_1_ext_sel;
  wire [31:0] extender_1_imm32, multiplexer_1_out;

  Extender extender_1 (.imm16(imm16), .sel_imm(encoder_1_ext_sel), .imm32(extender_1_imm32));
  Encoder encoder_1 (
    .in({opcode, funct}), .zero(alu_1_zero), .ALU_sel(encoder_1_alu_sel), .EXT_sel(encoder_1_ext_sel),
    .B_sel(encoder_1_b_sel), .PC_sel(PC_sel));
  ALU alu_1 (
    .cin(Cin), .A(A), .B(multiplexer_1_out), .ALU_sel(encoder_1_alu_sel), .co(Cout), .out(out),
    .zero(alu_1_zero));
  Multiplexer #(.width(32)) multiplexer_1 (
    .in0(B), .in1(extender_1_imm32), .out(multiplexer_1_out), .sel(encoder_1_b_sel));  // open: en
endmodule

// Mcod-18074021
module Encoder (
  input  [11:0] in,
  input  zero,
  output [1:0] ALU_sel,
  output [1:0] EXT_sel,
  output B_sel,
  output PC_sel
);

  wire not_1_out, or_2_out;
  wire [6:0] n7_mips_1_out_2;

  _7_MIPS u_7_mips_1 (.in_1(in), .out_2(n7_mips_1_out_2));
  nor nor_1 (ALU_sel[1], n7_mips_1_out_2[5], n7_mips_1_out_2[6], n7_mips_1_out_2[3], n7_mips_1_out_2[2], n7_mips_1_out_2[1], n7_mips_1_out_2[0]);
  not not_1 (not_1_out, EXT_sel[0]);
  or or_1 (ALU_sel[0], n7_mips_1_out_2[5], ALU_sel[1], n7_mips_1_out_2[0]);
  or or_2 (or_2_out, n7_mips_1_out_2[3], not_1_out);
  or or_3 (EXT_sel[0], n7_mips_1_out_2[2], n7_mips_1_out_2[1]);
  xor xor_1 (EXT_sel[1], n7_mips_1_out_2[4], or_2_out);
  or or_4 (B_sel, n7_mips_1_out_2[1], n7_mips_1_out_2[2], n7_mips_1_out_2[3], n7_mips_1_out_2[4]);
  and and_1 (PC_sel, n7_mips_1_out_2[0], zero);
endmodule

// Mdec-18074102
module _7_MIPS (
  input  [11:0] in_1,
  output [6:0] out_2
);

  wire decoder_1_out0, decoder_1_out1, decoder_1_out4, decoder_1_out5, decoder_2_out0, decoder_2_out3,
       decoder_2_out4, decoder_2_out5, decoder_2_out7, decoder_3_out4, decoder_4_out1, decoder_4_out3;

  Decoder #(.select(3)) decoder_1 (
    .out0(decoder_1_out0), .out1(decoder_1_out1), .out4(decoder_1_out4), .out5(decoder_1_out5),
    .sel(in_1[11:9]));  // open: out2, out3, out6, out7, en
  Decoder #(.select(3)) decoder_2 (
    .out0(decoder_2_out0), .out3(decoder_2_out3), .out4(decoder_2_out4), .out5(decoder_2_out5),
    .out7(decoder_2_out7), .sel(in_1[8:6]));  // open: out1, out2, out6, en
  Decoder #(.select(3)) decoder_3 (
    .out4(decoder_3_out4), .sel(in_1[5:3]));  // open: out0, out1, out2, out3, out5, out6, out7, en
  Decoder #(.select(3)) decoder_4 (
    .out1(decoder_4_out1), .out3(decoder_4_out3), .sel(in_1[2:0]));  // open: out0, out2, out4, out5, out6, out7, en
  and and_1 (out_2[6], decoder_1_out0, decoder_2_out0, decoder_3_out4, decoder_4_out1);
  and and_2 (out_2[5], decoder_1_out0, decoder_2_out0, decoder_3_out4, decoder_4_out3);
  and and_3 (out_2[4], decoder_1_out1, decoder_2_out5);
  and and_4 (out_2[3], decoder_1_out1, decoder_2_out7);
  and and_5 (out_2[2], decoder_1_out4, decoder_2_out3);
  and and_6 (out_2[1], decoder_1_out5, decoder_2_out3);
  and and_7 (out_2[0], decoder_2_out4, decoder_1_out0);
endmodule

// num-18074102
module Extender (
  input  [15:0] imm16,
  input  [1:0] sel_imm,
  output [31:0] imm32
);

  wire bitselector_1_out;
  wire [15:0] multiplexer_1_out;

  BitSelector #(.width(16)) bitselector_1 (.in(imm16), .out(bitselector_1_out), .sel(4'b1111));
  Multiplexer #(.width(16)) multiplexer_1 (
    .in0({16{1'b0}}), .in1({16{1'b1}}), .out(multiplexer_1_out), .sel(bitselector_1_out));  // open: en
  Multiplexer #(.select(2), .width(32)) multiplexer_2 (
    .in0({{16{1'b0}}, imm16}), .in1({multiplexer_1_out, imm16}), .in2({imm16, {16{1'b0}}}), .in3({32{1'b0}}),
    .out(imm32), .sel(sel_imm));  // open: en
endmodule

// 18074102 add1
module _1bfa (
  input  A,
  input  B,
  input  cin,
  output Sum,
  output co
);

  wire and_1_out, and_2_out, and_3_out, xor_1_out;

  xor xor_1 (xor_1_out, A, B);
  and and_1 (and_1_out, A, B);
  and and_2 (and_2_out, A, cin);
  and and_3 (and_3_out, B, cin);
  xor xor_2 (Sum, xor_1_out, cin);
  or or_1 (co, and_1_out, and_2_out, and_3_out);
endmodule

// 18074102 add4
module _4bfa (
  input  [3:0] in_1,
  input  [3:0] in_2,
  input  in_3,
  output [3:0] out_4,
  output out_5
);

  wire n1bfa_2_co, n1bfa_3_co, n1bfa_4_co;

  _1bfa u_1bfa_1 (.A(in_1[3]), .B(in_2[3]), .cin(n1bfa_2_co), .Sum(out_4[3]), .co(out_5));
  _1bfa u_1bfa_2 (.A(in_1[2]), .B(in_2[2]), .cin(n1bfa_3_co), .Sum(out_4[2]), .co(n1bfa_2_co));
  _1bfa u_1bfa_3 (.A(in_1[1]), .B(in_2[1]), .cin(n1bfa_4_co), .Sum(out_4[1]), .co(n1bfa_3_co));
  _1bfa u_1bfa_4 (.A(in_1[0]), .B(in_2[0]), .cin(in_3), .Sum(out_4[0]), .co(n1bfa_4_co));
endmodule

// 18074102 add32
module _32bfa (
  input  [31:0] A,
  input  [31:0] B,
  input  cin,
  output co,
  output [31:0] out
);

  wire n4bfa_2_out_5, n4bfa_3_out_5, n4bfa_4_out_5, n4bfa_5_out_5, n4bfa_6_out_5, n4bfa_7_out_5,
       n4bfa_8_out_5;

  _4bfa u_4bfa_1 (.in_1(A[31:28]), .in_2(B[31:28]), .out_4(out[31:28]), .out_5(co), .in_3(n4bfa_2_out_5));
  _4bfa u_4bfa_2 (.in_1(A[27:24]), .in_2(B[27:24]), .out_4(out[27:24]), .out_5(n4bfa_2_out_5), .in_3(n4bfa_3_out_5));
  _4bfa u_4bfa_3 (.in_1(A[23:20]), .in_2(B[23:20]), .out_4(out[23:20]), .out_5(n4bfa_3_out_5), .in_3(n4bfa_4_out_5));
  _4bfa u_4bfa_4 (.in_1(A[19:16]), .in_2(B[19:16]), .out_4(out[19:16]), .out_5(n4bfa_4_out_5), .in_3(n4bfa_5_out_5));
  _4bfa u_4bfa_5 (.in_1(A[15:12]), .in_2(B[15:12]), .out_4(out[15:12]), .out_5(n4bfa_5_out_5), .in_3(n4bfa_6_out_5));
  _4bfa u_4bfa_6 (.in_1(A[11:8]), .in_2(B[11:8]), .out_4(out[11:8]), .out_5(n4bfa_6_out_5), .in_3(n4bfa_7_out_5));
  _4bfa u_4bfa_7 (.in_1(A[7:4]), .in_2(B[7:4]), .out_4(out[7:4]), .out_5(n4bfa_7_out_5), .in_3(n4bfa_8_out_5));
  _4bfa u_4bfa_8 (.in_1(A[3:0]), .in_2(B[3:0]), .out_4(out[3:0]), .out_5(n4bfa_8_out_5), .in_3(cin));
endmodule

// 18074102 sub32
module _32bfs (
  input  [31:0] A,
  input  [31:0] B,
  input  Cin,
  output [31:0] out,
  output co
);

  wire [31:0] n32bfa_1_out, not_1_out;

  assign not_1_out = ~A;  // NOT_Gate not_1, 32 bits wide
  _32bfa u_32bfa_1 (.A(not_1_out), .B(B), .out(n32bfa_1_out), .co(co), .cin(Cin));
  assign out = ~n32bfa_1_out;  // NOT_Gate not_2, 32 bits wide
endmodule

// ALU-18074102
module ALU (
  input  cin,
  input  [31:0] A,
  input  [31:0] B,
  input  [1:0] ALU_sel,
  output co,
  output [31:0] out,
  output zero
);

  wire n32bfa_1_co, n32bfs_1_co;
  wire [31:0] and_1_out, n32bfa_1_out, n32bfs_1_out, or_1_out;

  _32bfs u_32bfs_1 (.A(A), .B(B), .Cin(cin), .out(n32bfs_1_out), .co(n32bfs_1_co));
  _32bfa u_32bfa_1 (.A(A), .B(B), .out(n32bfa_1_out), .co(n32bfa_1_co), .cin(cin));
  assign and_1_out = A & B;  // AND_Gate and_1, 32 bits wide
  assign or_1_out = A | B;  // OR_Gate or_1, 32 bits wide
  Multiplexer #(.select(2), .width(32)) multiplexer_1 (
    .in0(n32bfa_1_out), .in1(n32bfs_1_out), .in2(and_1_out), .in3(or_1_out), .out(out), .sel(ALU_sel));  // open: en
  Multiplexer #(.select(2)) multiplexer_2 (
    .in0(n32bfa_1_co), .in1(n32bfs_1_co), .in2(1'b0), .in3(1'b0), .out(co), .sel(ALU_sel));  // open: en
  nor nor_1 (zero, out[15], out[0], out[1], out[2], out[3], out[4], out[5], out[6], out[7], out[8], out[9], out[10], out[11], out[12], out[13], out[14], out[16], out[17], out[18], out[19], out[20], out[21], out[22], out[23], out[24], out[25], out[26], out[27], out[28], out[29], out[30], out[31]);
endmodule
