// Logisim project expd.circ as structural Verilog: 1 circuit, main circuit main
module main (
  input  [15:0] in_1,
  input  [1:0] in_2,
  output [31:0] out_3
);

  wire bitselector_1_out;
  wire [15:0] multiplexer_1_out;

  BitSelector #(.width(16)) bitselector_1 (.in(in_1), .out(bitselector_1_out), .sel(4'b1111));
  Multiplexer #(.width(16)) multiplexer_1 (
    .in0({16{1'b0}}), .in1({16{1'b1}}), .out(multiplexer_1_out), .sel(bitselector_1_out));  // open: en
  Multiplexer #(.select(2), .width(32)) multiplexer_2 (
    .in0({{16{1'b0}}, in_1}), .in1({multiplexer_1_out, in_1}), .in2({in_1, {16{1'b0}}}), .in3({32{1'b0}}),
    .out(out_3), .sel(in_2));  // open: en
endmodule
